# Fritzing sketch Circuit_Design (saved by Fritzing 1.0.6)

parts:
  RHT1 = Humidity and Temperature Sensor RHT03
  Mod1 = Amica NodeMCU DEVKIT 1.0
  DotStar1 = DotStar LED Strip [mn=Adafruit mpn=2239 part_number=2239]
  Grove1 = Grove OLED 128x96
  Part2 = Barometric Pressure Sensor - BMP180 Breakout (GY-68)
  J1 = Piezo Speaker
  Part1 = Soil Moisture Sensor

nets:
  VCC: RHT1.Vcc, Mod1.pin_10, Mod1.pin_26, Grove1.VCC, Part2.VCC, Part1.VCC
  N1: RHT1.Data-signal, Mod1.pin8
  GND: RHT1.GND_1, RHT1.GND_2, Mod1.pin2, Mod1.pin_9, Mod1.pin_25, Mod1.pin_29, DotStar1.GND, Grove1.GND, Part2.GND, J1.pin1, Part1.GND
  N2: Mod1.pin5, J1.pin2
  N3: Mod1.pin7, Mod1.pin_16, Part1.SIG
  N4: Mod1.pin_11, DotStar1.DO
  N5: Mod1.pin_13, Grove1.SDA, Part2.SDA
  N6: Mod1.pin_14, Grove1.SCL, Part2.SCL
  N7: Mod1.pin_30, DotStar1.+5V

notes:
  DHT11
  OLED
  Moisture  (Rain Detector)
  NeoPixel LEDs
  Buzzer
  BMP280
  ESP8266
